# Fritzing sketch Feather32JTAG (saved by Fritzing 0.9.4)
circuit board: 7.84573cm x 4.87697cm
breadboards: 1

parts:
  Feather_32 = Adafruit HUZZAH32 ESP32 Feather [part_number="Adafruit #3405"]
  JTAG = Generic shrouded header - 10 pins [form="♂ (shrouded male)" package=THT]
  J3 = female pin header, 12 pins [form="♀ (female)"]
  J4 = female pin header, 16 pins [form="♀ (female)"]

nets:
  N1: Feather_32.IO21, J4.pin1
  N2: Feather_32.IO17, J4.pin2
  N3: Feather_32.IO16, J4.pin3
  N4: Feather_32.MISO, J4.pin4
  N5: Feather_32.MOSI, J4.pin5
  N6: Feather_32.SCK, J4.pin6
  N7: Feather_32.A5_IO4, J4.pin7
  N8: Feather_32.A4_IO36, J4.pin8
  N9: Feather_32.A3_I39, J4.pin9
  N10: Feather_32.A2_I34, J4.pin10
  N11: Feather_32.A1_DAC1, J4.pin11
  N12: Feather_32.A0_DAC2, J4.pin12
  N13: Feather_32.GND, JTAG.pin3, J4.pin13
  N14: Feather_32.N/C, J4.pin14
  N15: Feather_32.3.3V, JTAG.pin1, J4.pin15
  N16: Feather_32.RESET, J4.pin16
  N17: Feather_32.VBAT, J3.pin12
  N18: Feather_32.EN, J3.pin11
  N19: Feather_32.VBUS, J3.pin10
  N20: Feather_32.IO13_A12, JTAG.pin4, J3.pin9
  N21: Feather_32.IO12_A11, JTAG.pin6, J3.pin8
  N22: Feather_32.IO27_A10, J3.pin7
  N23: Feather_32.IO33_A9, J3.pin6
  N24: Feather_32.IO15_A8, JTAG.pin5, J3.pin5
  N25: Feather_32.IO32_A7, J3.pin4
  N26: Feather_32.IO14_A6, JTAG.pin2, J3.pin3
  N27: Feather_32.SCL, J3.pin2
  N28: Feather_32.SDA, J3.pin1

notes:
  v0.0.1
  Feather JTAG breakout

custom parts:
  Generic shrouded header - 10 pins: Generic shrouded header
